# Fritzing sketch dshop_counter (saved by Fritzing 0.9.3b)
breadboards: 1

parts:
  Raspberry_Pi_1 = Raspberry Pi 3 [part_number=RPI-3-V1.2]
  R1 = Resistor [tolerance=±5% resistance=1k package=THT]
  S2 = Round Pushbutton
  Imagine_as_PIR_sensor = PNP-Transistor [package="TO92 [THT]"]
  LED1 = LED - 5mm [color="Blue (525nm)" package="5 mm [THT]"]
  R2 = Resistor [tolerance=±5% resistance=220 package=THT]
  R3 = Resistor [tolerance=±5% resistance=220 package=THT]
  LED2 = LED - 5mm [color="Green (560nm)" package="5 mm [THT]"]

nets:
  N1: Raspberry_Pi_1.3v3, R1.Pin_1
  N2: Raspberry_Pi_1.GND, S2.leg0, Imagine_as_PIR_sensor.E, LED1.cathode, LED2.cathode
  N3: Raspberry_Pi_1.GPIO26, R3.Pin_0
  N4: Raspberry_Pi_1.GPIO16, R1.Pin_0, S2.leg1
  N5: Raspberry_Pi_1.GPIO23, Imagine_as_PIR_sensor.B
  N6: Raspberry_Pi_1.GPIO18, R2.Pin_0
  N7: LED1.anode, R2.Pin_1
  N8: R3.Pin_1, LED2.anode
